// Logisim project Relógio_Digital_no_Logisim.circ as structural Verilog: 1 circuit, main circuit main
module main (
);

  wire alterar_hora_dezena, alterar_hora_unidade, alterar_min_dezena, alterar_min_unidade,
       alterar_seg_dezena, alterar_seg_unidade, and_1_out, and_2_out, and_3_out, and_4_out, and_5_out,
       bcd_to_7_segment_decoder_1_p1, bcd_to_7_segment_decoder_1_p2, bcd_to_7_segment_decoder_1_p3,
       bcd_to_7_segment_decoder_1_p4, bcd_to_7_segment_decoder_1_p6, bcd_to_7_segment_decoder_1_p7,
       bcd_to_7_segment_decoder_1_p8, bcd_to_7_segment_decoder_2_p1, bcd_to_7_segment_decoder_2_p2,
       bcd_to_7_segment_decoder_2_p3, bcd_to_7_segment_decoder_2_p4, bcd_to_7_segment_decoder_2_p6,
       bcd_to_7_segment_decoder_2_p7, bcd_to_7_segment_decoder_2_p8, bcd_to_7_segment_decoder_3_p1,
       bcd_to_7_segment_decoder_3_p2, bcd_to_7_segment_decoder_3_p3, bcd_to_7_segment_decoder_3_p4,
       bcd_to_7_segment_decoder_3_p6, bcd_to_7_segment_decoder_3_p7, bcd_to_7_segment_decoder_3_p8,
       bcd_to_7_segment_decoder_4_p1, bcd_to_7_segment_decoder_4_p2, bcd_to_7_segment_decoder_4_p3,
       bcd_to_7_segment_decoder_4_p4, bcd_to_7_segment_decoder_4_p6, bcd_to_7_segment_decoder_4_p7,
       bcd_to_7_segment_decoder_4_p8, bcd_to_7_segment_decoder_5_p1, bcd_to_7_segment_decoder_5_p2,
       bcd_to_7_segment_decoder_5_p3, bcd_to_7_segment_decoder_5_p4, bcd_to_7_segment_decoder_5_p6,
       bcd_to_7_segment_decoder_5_p7, bcd_to_7_segment_decoder_5_p8, bcd_to_7_segment_decoder_6_p1,
       bcd_to_7_segment_decoder_6_p2, bcd_to_7_segment_decoder_6_p3, bcd_to_7_segment_decoder_6_p4,
       bcd_to_7_segment_decoder_6_p6, bcd_to_7_segment_decoder_6_p7, bcd_to_7_segment_decoder_6_p8,
       button_7_out, j_k_ff_5_qn, j_k_ff_10_qn, j_k_ff_11_qn, not_1_out, or_1_out, or_2_out, or_3_out,
       or_4_out, or_5_out, or_6_out, or_7_out, or_8_out, or_9_out, or_10_out, quando_3_out, quando_4_out,
       quando_10_out, quando_24h_out;
  wire [1:0] hora_dezena;
  wire [2:0] min_dezena, seg_dezena;
  wire [3:0] hora_unidade, min_unidade, seg_unidade;

  Button button_1 (.out(alterar_seg_unidade));
  Button button_2 (.out(alterar_seg_dezena));
  Button button_3 (.out(alterar_min_unidade));
  Button button_4 (.out(alterar_min_dezena));
  Button button_5 (.out(alterar_hora_unidade));
  Button button_6 (.out(alterar_hora_dezena));
  or or_1 (or_1_out, or_8_out, or_6_out);
  Button button_7 (.out(button_7_out));
  _7_Segment_Display u_7_segment_display_1 (
    .g(bcd_to_7_segment_decoder_1_p1), .f(bcd_to_7_segment_decoder_1_p3), .a(bcd_to_7_segment_decoder_1_p6),
    .b(bcd_to_7_segment_decoder_1_p8), .e(bcd_to_7_segment_decoder_1_p2), .d(bcd_to_7_segment_decoder_1_p4),
    .c(bcd_to_7_segment_decoder_1_p7));  // open: dp
  or or_2 (or_2_out, button_7_out, alterar_seg_unidade, or_6_out);
  or or_3 (or_3_out, and_2_out, alterar_seg_dezena);
  J_K_Flip_Flop #(.trigger("falling")) j_k_ff_1 (
    .J(1'b1), .K(1'b1), .clk(or_2_out), .Q(seg_unidade[0]), .reset(or_4_out));  // open: Qn, preset
  or or_4 (or_4_out, or_6_out, or_1_out, and_2_out);
  J_K_Flip_Flop #(.trigger("falling")) j_k_ff_2 (
    .J(1'b1), .K(1'b1), .clk(or_3_out), .Q(seg_dezena[0]), .reset(and_3_out));  // open: Qn, preset
  and and_1 (and_1_out, quando_10_out, not_1_out);
  // BCD_to_7_Segment_decoder bcd_to_7_segment_decoder_1: pin names not known; wires that end beside it: bcd_to_7_segment_decoder_1_p1, bcd_to_7_segment_decoder_1_p2, bcd_to_7_segment_decoder_1_p3, bcd_to_7_segment_decoder_1_p4, {2'b00, hora_dezena}, bcd_to_7_segment_decoder_1_p6, bcd_to_7_segment_decoder_1_p7, bcd_to_7_segment_decoder_1_p8
  J_K_Flip_Flop #(.trigger("falling")) j_k_ff_3 (
    .J(1'b1), .K(1'b1), .clk(seg_unidade[0]), .Q(seg_unidade[1]), .reset(or_4_out));  // open: Qn, preset
  J_K_Flip_Flop #(.trigger("falling")) j_k_ff_4 (
    .J(1'b1), .K(1'b1), .clk(seg_dezena[0]), .Q(seg_dezena[1]), .reset(and_3_out));  // open: Qn, preset
  J_K_Flip_Flop #(.trigger("falling")) j_k_ff_5 (
    .J(1'b1), .K(1'b1), .clk(or_5_out), .Q(hora_dezena[0]), .Qn(j_k_ff_5_qn), .reset(or_6_out));  // open: preset
  or or_5 (or_5_out, alterar_hora_dezena, and_1_out);
  or or_6 (or_6_out, quando_24h_out, quando_3_out);
  not not_1 (not_1_out, quando_24h_out);
  _7_Segment_Display u_7_segment_display_2 (
    .g(bcd_to_7_segment_decoder_2_p1), .f(bcd_to_7_segment_decoder_2_p3), .a(bcd_to_7_segment_decoder_2_p6),
    .b(bcd_to_7_segment_decoder_2_p8), .e(bcd_to_7_segment_decoder_2_p2), .d(bcd_to_7_segment_decoder_2_p4),
    .c(bcd_to_7_segment_decoder_2_p7));  // open: dp
  J_K_Flip_Flop #(.trigger("falling")) j_k_ff_6 (
    .J(1'b1), .K(1'b1), .clk(seg_unidade[1]), .Q(seg_unidade[2]), .reset(or_4_out));  // open: Qn, preset
  J_K_Flip_Flop #(.trigger("falling")) j_k_ff_7 (
    .J(1'b1), .K(1'b1), .clk(seg_dezena[1]), .Q(seg_dezena[2]), .reset(and_3_out));  // open: Qn, preset
  and quando_3 (quando_3_out, hora_dezena[0], hora_dezena[1]);
  // BCD_to_7_Segment_decoder bcd_to_7_segment_decoder_2: pin names not known; wires that end beside it: bcd_to_7_segment_decoder_2_p1, bcd_to_7_segment_decoder_2_p2, bcd_to_7_segment_decoder_2_p3, bcd_to_7_segment_decoder_2_p4, hora_unidade, bcd_to_7_segment_decoder_2_p6, bcd_to_7_segment_decoder_2_p7, bcd_to_7_segment_decoder_2_p8
  and and_2 (and_2_out, seg_unidade[1], seg_unidade[3]);
  and and_3 (and_3_out, seg_dezena[1], seg_dezena[2]);
  J_K_Flip_Flop #(.trigger("falling")) j_k_ff_8 (
    .J(1'b1), .K(1'b1), .clk(hora_dezena[0]), .Q(hora_dezena[1]), .reset(or_6_out));  // open: Qn, preset
  LED led_1 (.in(1'b1));
  LED led_2 (.in(1'b1));
  J_K_Flip_Flop #(.trigger("falling")) j_k_ff_9 (
    .J(1'b1), .K(1'b1), .clk(seg_unidade[2]), .Q(seg_unidade[3]), .reset(or_4_out));  // open: Qn, preset
  and quando_24h (quando_24h_out, j_k_ff_5_qn, hora_dezena[1], quando_4_out);
  _7_Segment_Display u_7_segment_display_3 (
    .g(bcd_to_7_segment_decoder_3_p1), .f(bcd_to_7_segment_decoder_3_p3), .a(bcd_to_7_segment_decoder_3_p6),
    .b(bcd_to_7_segment_decoder_3_p8), .e(bcd_to_7_segment_decoder_3_p2), .d(bcd_to_7_segment_decoder_3_p4),
    .c(bcd_to_7_segment_decoder_3_p7));  // open: dp
  // BCD_to_7_Segment_decoder bcd_to_7_segment_decoder_3: pin names not known; wires that end beside it: bcd_to_7_segment_decoder_3_p1, bcd_to_7_segment_decoder_3_p2, bcd_to_7_segment_decoder_3_p3, bcd_to_7_segment_decoder_3_p4, {1'b0, min_dezena}, bcd_to_7_segment_decoder_3_p6, bcd_to_7_segment_decoder_3_p7, bcd_to_7_segment_decoder_3_p8
  _7_Segment_Display u_7_segment_display_4 (
    .g(bcd_to_7_segment_decoder_4_p1), .f(bcd_to_7_segment_decoder_4_p3), .a(bcd_to_7_segment_decoder_4_p6),
    .b(bcd_to_7_segment_decoder_4_p8), .e(bcd_to_7_segment_decoder_4_p2), .d(bcd_to_7_segment_decoder_4_p4),
    .c(bcd_to_7_segment_decoder_4_p7));  // open: dp
  or or_7 (or_7_out, and_5_out, alterar_hora_unidade);
  // BCD_to_7_Segment_decoder bcd_to_7_segment_decoder_4: pin names not known; wires that end beside it: bcd_to_7_segment_decoder_4_p1, bcd_to_7_segment_decoder_4_p2, bcd_to_7_segment_decoder_4_p3, bcd_to_7_segment_decoder_4_p4, min_unidade, bcd_to_7_segment_decoder_4_p6, bcd_to_7_segment_decoder_4_p7, bcd_to_7_segment_decoder_4_p8
  J_K_Flip_Flop #(.trigger("falling")) j_k_ff_10 (
    .J(1'b1), .K(1'b1), .clk(or_7_out), .Q(hora_unidade[0]), .Qn(j_k_ff_10_qn), .reset(or_8_out));  // open: preset
  or or_8 (or_8_out, quando_24h_out, quando_10_out);
  LED led_3 (.in(1'b1));
  LED led_4 (.in(1'b1));
  J_K_Flip_Flop #(.trigger("falling")) j_k_ff_11 (
    .J(1'b1), .K(1'b1), .clk(hora_unidade[0]), .Q(hora_unidade[1]), .Qn(j_k_ff_11_qn), .reset(or_8_out));  // open: preset
  _7_Segment_Display u_7_segment_display_5 (
    .g(bcd_to_7_segment_decoder_5_p1), .f(bcd_to_7_segment_decoder_5_p3), .a(bcd_to_7_segment_decoder_5_p6),
    .b(bcd_to_7_segment_decoder_5_p8), .e(bcd_to_7_segment_decoder_5_p2), .d(bcd_to_7_segment_decoder_5_p4),
    .c(bcd_to_7_segment_decoder_5_p7));  // open: dp
  J_K_Flip_Flop #(.trigger("falling")) j_k_ff_12 (
    .J(1'b1), .K(1'b1), .clk(or_9_out), .Q(min_unidade[0]), .reset(and_4_out));  // open: Qn, preset
  or or_9 (or_9_out, alterar_min_unidade, and_3_out);
  J_K_Flip_Flop #(.trigger("falling")) j_k_ff_13 (
    .J(1'b1), .K(1'b1), .clk(or_10_out), .Q(min_dezena[0]), .reset(and_5_out));  // open: Qn, preset
  or or_10 (or_10_out, and_4_out, alterar_min_dezena);
  J_K_Flip_Flop #(.trigger("falling")) j_k_ff_14 (
    .J(1'b1), .K(1'b1), .clk(hora_unidade[1]), .Q(hora_unidade[2]), .reset(or_8_out));  // open: Qn, preset
  and quando_4 (quando_4_out, j_k_ff_10_qn, j_k_ff_11_qn, hora_unidade[2]);
  // BCD_to_7_Segment_decoder bcd_to_7_segment_decoder_5: pin names not known; wires that end beside it: bcd_to_7_segment_decoder_5_p1, bcd_to_7_segment_decoder_5_p2, bcd_to_7_segment_decoder_5_p3, bcd_to_7_segment_decoder_5_p4, {1'b0, seg_dezena}, bcd_to_7_segment_decoder_5_p6, bcd_to_7_segment_decoder_5_p7, bcd_to_7_segment_decoder_5_p8
  _7_Segment_Display u_7_segment_display_6 (
    .g(bcd_to_7_segment_decoder_6_p1), .f(bcd_to_7_segment_decoder_6_p3), .a(bcd_to_7_segment_decoder_6_p6),
    .b(bcd_to_7_segment_decoder_6_p8), .e(bcd_to_7_segment_decoder_6_p2), .d(bcd_to_7_segment_decoder_6_p4),
    .c(bcd_to_7_segment_decoder_6_p7));  // open: dp
  J_K_Flip_Flop #(.trigger("falling")) j_k_ff_15 (
    .J(1'b1), .K(1'b1), .clk(min_unidade[0]), .Q(min_unidade[1]), .reset(and_4_out));  // open: Qn, preset
  J_K_Flip_Flop #(.trigger("falling")) j_k_ff_16 (
    .J(1'b1), .K(1'b1), .clk(min_dezena[0]), .Q(min_dezena[1]), .reset(and_5_out));  // open: Qn, preset
  J_K_Flip_Flop #(.trigger("falling")) j_k_ff_17 (
    .J(1'b1), .K(1'b1), .clk(hora_unidade[2]), .Q(hora_unidade[3]), .reset(or_8_out));  // open: Qn, preset
  J_K_Flip_Flop #(.trigger("falling")) j_k_ff_18 (
    .J(1'b1), .K(1'b1), .clk(min_unidade[1]), .Q(min_unidade[2]), .reset(and_4_out));  // open: Qn, preset
  J_K_Flip_Flop #(.trigger("falling")) j_k_ff_19 (
    .J(1'b1), .K(1'b1), .clk(min_dezena[1]), .Q(min_dezena[2]), .reset(and_5_out));  // open: Qn, preset
  and quando_10 (quando_10_out, hora_unidade[1], hora_unidade[3]);
  // BCD_to_7_Segment_decoder bcd_to_7_segment_decoder_6: pin names not known; wires that end beside it: bcd_to_7_segment_decoder_6_p1, bcd_to_7_segment_decoder_6_p2, bcd_to_7_segment_decoder_6_p3, bcd_to_7_segment_decoder_6_p4, seg_unidade, bcd_to_7_segment_decoder_6_p6, bcd_to_7_segment_decoder_6_p7, bcd_to_7_segment_decoder_6_p8
  and and_4 (and_4_out, min_unidade[1], min_unidade[3]);
  and and_5 (and_5_out, min_dezena[1], min_dezena[2]);
  J_K_Flip_Flop #(.trigger("falling")) j_k_ff_20 (
    .J(1'b1), .K(1'b1), .clk(min_unidade[2]), .Q(min_unidade[3]), .reset(and_4_out));  // open: Qn, preset
endmodule
